// Logisim project comparadorBinarios.circ as structural Verilog: 1 circuit, main circuit main
module main (
  input  in_1,
  input  in_2,
  input  in_3,
  input  in_4,
  input  in_5,
  input  in_6,
  input  in_7,
  input  in_8,
  input  in_9,
  input  in_10,
  input  in_11,
  input  in_12,
  input  in_13,
  input  in_14,
  input  in_15,
  input  in_16,
  output out_17
);

  wire or_1_out, or_2_out, or_3_out, or_4_out, or_5_out, or_6_out, xor_1_out, xor_2_out, xor_3_out,
       xor_4_out, xor_5_out, xor_6_out, xor_7_out, xor_8_out;

  xor xor_1 (xor_1_out, in_1, in_9);
  xor xor_2 (xor_2_out, in_2, in_10);
  xor xor_3 (xor_3_out, in_3, in_11);
  xor xor_4 (xor_4_out, in_4, in_12);
  xor xor_5 (xor_5_out, in_5, in_13);
  xor xor_6 (xor_6_out, in_6, in_14);
  xor xor_7 (xor_7_out, in_7, in_15);
  xor xor_8 (xor_8_out, in_8, in_16);
  or or_1 (or_1_out, xor_1_out, xor_2_out);
  or or_2 (or_2_out, or_1_out, xor_3_out);
  or or_3 (or_3_out, or_2_out, xor_4_out);
  or or_4 (or_4_out, or_3_out, xor_5_out);
  or or_5 (or_5_out, or_4_out, xor_6_out);
  or or_6 (or_6_out, or_5_out, xor_7_out);
  or or_7 (out_17, or_6_out, xor_8_out);
endmodule
