// Logisim project multiplicador.circ as structural Verilog: 3 circuits, main circuit Half Adder
module Half_Adder (
  input  in_1,
  input  in_2,
  output S1,
  output Cout
);

  xor xor_1 (S1, in_2, in_1);
  and and_1 (Cout, in_2, in_1);
endmodule

module Full_Adder (
  input  Cin,
  input  in_2,
  input  in_3,
  output Saida,
  output Cout
);

  wire and_1_out, and_2_out, and_3_out, or_1_out, xor_2_out;

  and and_1 (and_1_out, Cin, in_2);
  and and_2 (and_2_out, in_3, in_2);
  and and_3 (and_3_out, in_3, Cin);
  xor xor_1 (Saida, Cin, xor_2_out);
  xor xor_2 (xor_2_out, in_2, in_3);
  or or_1 (or_1_out, and_1_out, and_2_out);
  or or_2 (Cout, or_1_out, and_3_out);
endmodule

module Multiplicador (
  input  A2,
  input  A1,
  input  A0,
  input  B2,
  input  B1,
  input  B0,
  output out_7,
  output out_8,
  output out_9,
  output out_10,
  output out_11,
  output out_12
);

  wire and_1_out, and_2_out, and_3_out, and_4_out, and_5_out, and_6_out, and_7_out, and_8_out,
       full_adder_1_cout, full_adder_1_saida, full_adder_2_cout, half_adder_1_cout, half_adder_2_cout,
       half_adder_3_cout, half_adder_3_s1;

  and and_1 (and_1_out, A1, B0);
  and and_2 (and_2_out, A0, B1);
  and and_3 (and_3_out, A2, B0);
  and and_4 (and_4_out, A1, B1);
  and and_5 (and_5_out, A0, B2);
  and and_6 (and_6_out, A2, B1);
  and and_7 (and_7_out, A1, B2);
  and and_8 (and_8_out, A2, B2);
  Half_Adder half_adder_1 (.in_1(and_1_out), .in_2(and_2_out), .S1(out_11), .Cout(half_adder_1_cout));
  Full_Adder full_adder_1 (
    .Cin(half_adder_1_cout), .in_2(and_3_out), .in_3(and_4_out), .Saida(full_adder_1_saida),
    .Cout(full_adder_1_cout));
  Half_Adder half_adder_2 (.in_1(full_adder_1_saida), .in_2(and_5_out), .S1(out_10), .Cout(half_adder_2_cout));
  Half_Adder half_adder_3 (
    .in_1(full_adder_1_cout), .in_2(half_adder_2_cout), .S1(half_adder_3_s1), .Cout(half_adder_3_cout));
  Full_Adder full_adder_2 (
    .Cin(half_adder_3_s1), .in_2(and_6_out), .in_3(and_7_out), .Saida(out_9), .Cout(full_adder_2_cout));
  Full_Adder full_adder_3 (
    .Cin(half_adder_3_cout), .in_2(full_adder_2_cout), .in_3(and_8_out), .Saida(out_8), .Cout(out_7));
  and and_9 (out_12, A0, B0);
endmodule
