// Logisim project paridadePar.circ as structural Verilog: 1 circuit, main circuit main
module main (
  input  a,
  input  b,
  input  c,
  input  d,
  input  e,
  input  f,
  input  g,
  input  h,
  output x
);

  wire xor_1_out, xor_2_out, xor_3_out, xor_4_out, xor_5_out, xor_6_out;

  xor xor_1 (xor_1_out, a, b);
  xor xor_2 (xor_2_out, xor_1_out, c);
  xor xor_3 (xor_3_out, xor_2_out, d);
  xor xor_4 (xor_4_out, xor_3_out, e);
  xor xor_5 (xor_5_out, xor_4_out, f);
  xor xor_6 (xor_6_out, xor_5_out, g);
  xnor xnor_1 (x, xor_6_out, h);
endmodule
