// Logisim project pratica 03.circ as structural Verilog: 6 circuits, main circuit main
module main (
  input  A,
  input  B,
  input  C,
  input  D,
  output x
);

  wire and_1_out, and_2_out, and_3_out, and_4_out, nand_1_out, not_1_out, not_2_out;

  and and_1 (and_1_out, A, B);
  not not_1 (not_1_out, A);
  and and_2 (and_2_out, not_1_out, C);
  not not_2 (not_2_out, B);
  and and_3 (and_3_out, not_2_out, C);
  nand nand_1 (nand_1_out, B, C);
  and and_4 (and_4_out, nand_1_out, D);
  or or_1 (x, and_1_out, and_2_out, and_3_out, and_4_out);

  // Notes on the sheet:
  //   1.
endmodule

module _2_A (
  input  A,
  input  B,
  input  C,
  output x
);

  wire and_1_out, not_1_out, xor_1_out;

  not not_1 (not_1_out, B);
  xor xor_1 (xor_1_out, A, not_1_out);
  and and_1 (and_1_out, A, C);
  or or_1 (x, xor_1_out, and_1_out);

  // Notes on the sheet:
  //   2.A
endmodule

module _2_B (
  input  A,
  input  B,
  input  C,
  output x
);

  wire and_1_out, and_2_out, not_1_out;

  not not_1 (not_1_out, B);
  and and_1 (and_1_out, A, B);
  and and_2 (and_2_out, not_1_out, C);
  or or_1 (x, and_1_out, and_2_out);

  // Notes on the sheet:
  //   2.B
endmodule

module _3 (
  input  C,
  input  C_2,
  input  C_3,
  input  D,
  input  D_2,
  input  D_3,
  input  C_4,
  input  C_5,
  input  D_4,
  output out_10,
  output out_11,
  output out_12,
  output out_13,
  output out_14
);

  and and_1 (out_10, C, D);
  nand nand_1 (out_13, C_4, D_4);
  or or_1 (out_11, C_2, D_2);
  xor xor_1 (out_12, C_3, D_3);

  assign out_14 = C_5;

  // Notes on the sheet:
  //   3.
  //   Proposição P
  //   Proposição B
  //   Proposição R
  //   Proposição S
  //   Proposição M
endmodule

module _4 (
  input  A,
  input  B,
  input  C,
  input  D,
  output x
);

  wire and_1_out, and_2_out, and_3_out, not_1_out, not_2_out;

  not not_1 (not_1_out, C);
  and and_1 (and_1_out, not_1_out, D);
  not not_2 (not_2_out, A);
  and and_2 (and_2_out, not_2_out, B, C);
  and and_3 (and_3_out, A, D);
  or or_1 (x, and_1_out, and_2_out, and_3_out);

  // Notes on the sheet:
  //   4.B
  //   ~CD + ~ABC + AD
endmodule

module _4_a (
  input  A,
  input  B,
  input  C,
  input  D,
  output x
);

  wire and_1_out, and_2_out, and_3_out;

  and and_1 (and_1_out, B, C);
  and and_2 (and_2_out, A, D);
  and and_3 (and_3_out, A, B);
  or or_1 (x, and_1_out, and_2_out, and_3_out);

  // Notes on the sheet:
  //   4.A
  //   BC + AD +AB
endmodule
