// Logisim project pratica display.circ as structural Verilog: 8 circuits, main circuit main
module main (
  input  in_1,
  input  in_2,
  input  in_3,
  input  in_4
);

  wire a_1_x, b_1_x, c_1_x, d_1_x, e_1_x, f_1_x, g_1_x;

  a a_1 (.a(in_1), .b(in_2), .c(in_3), .d(in_4), .x(a_1_x));
  b b_1 (.a(in_1), .b(in_2), .c(in_3), .d(in_4), .x(b_1_x));
  c c_1 (.a(in_1), .b(in_2), .c(in_3), .d(in_4), .x(c_1_x));
  d d_1 (.a(in_1), .b(in_2), .c(in_3), .d(in_4), .x(d_1_x));
  e e_1 (.a(in_1), .b(in_2), .c(in_3), .d(in_4), .x(e_1_x));
  f f_1 (.a(in_1), .b(in_2), .c(in_3), .d(in_4), .x(f_1_x));
  g g_1 (.a(in_1), .b(in_2), .c(in_3), .d(in_4), .x(g_1_x));
  _7_Segment_Display u_7_segment_display_1 (
    .g(g_1_x), .f(f_1_x), .a(a_1_x), .b(b_1_x), .e(e_1_x), .d(d_1_x), .c(c_1_x));  // open: dp
endmodule

module a (
  input  a,
  input  b,
  input  c,
  input  d,
  output x
);

  wire and_1_out, and_2_out, and_3_out, and_4_out, and_5_out, and_6_out, not_1_out, not_2_out, not_3_out,
       not_4_out, not_5_out, not_6_out, not_7_out;

  not not_1 (not_1_out, b);
  and and_1 (and_1_out, not_1_out, not_2_out);
  not not_2 (not_2_out, d);
  not not_3 (not_3_out, a);
  and and_2 (and_2_out, not_3_out, c);
  not not_4 (not_4_out, a);
  and and_3 (and_3_out, not_4_out, b, d);
  and and_4 (and_4_out, b, c);
  not not_5 (not_5_out, b);
  and and_5 (and_5_out, a, not_5_out, not_6_out);
  not not_6 (not_6_out, c);
  and and_6 (and_6_out, a, not_7_out);
  not not_7 (not_7_out, d);
  or or_1 (x, and_1_out, and_2_out, and_3_out, and_4_out, and_5_out, and_6_out);
endmodule

module b (
  input  a,
  input  b,
  input  c,
  input  d,
  output x
);

  wire and_1_out, and_2_out, and_3_out, and_4_out, and_5_out, not_1_out, not_2_out, not_3_out, not_4_out,
       not_5_out, not_6_out, not_7_out, not_8_out, not_9_out;

  not not_1 (not_1_out, a);
  and and_1 (and_1_out, not_1_out, not_2_out);
  not not_2 (not_2_out, b);
  not not_3 (not_3_out, a);
  not not_4 (not_4_out, c);
  and and_2 (and_2_out, not_3_out, not_4_out, not_5_out);
  not not_5 (not_5_out, d);
  not not_6 (not_6_out, b);
  and and_3 (and_3_out, not_6_out, not_7_out);
  not not_7 (not_7_out, d);
  not not_8 (not_8_out, a);
  and and_4 (and_4_out, not_8_out, c, d);
  not not_9 (not_9_out, c);
  and and_5 (and_5_out, a, not_9_out, d);
  or or_1 (x, and_1_out, and_2_out, and_3_out, and_4_out, and_5_out);
endmodule

module c (
  input  a,
  input  b,
  input  c,
  input  d,
  output x
);

  wire and_1_out, and_2_out, and_3_out, and_4_out, and_5_out, not_1_out, not_2_out, not_3_out, not_4_out,
       not_5_out, not_6_out;

  not not_1 (not_1_out, a);
  and and_1 (and_1_out, not_1_out, not_2_out);
  not not_2 (not_2_out, c);
  not not_3 (not_3_out, a);
  and and_2 (and_2_out, not_3_out, d);
  not not_4 (not_4_out, c);
  and and_3 (and_3_out, not_4_out, d);
  not not_5 (not_5_out, a);
  and and_4 (and_4_out, not_5_out, b);
  and and_5 (and_5_out, a, not_6_out);
  not not_6 (not_6_out, b);
  or or_1 (x, and_1_out, and_2_out, and_3_out, and_4_out, and_5_out);
endmodule

module d (
  input  a,
  input  b,
  input  c,
  input  d,
  output x
);

  wire and_1_out, and_2_out, and_3_out, and_4_out, and_5_out, not_1_out, not_2_out, not_3_out, not_4_out,
       not_5_out, not_6_out, not_7_out, not_8_out;

  not not_1 (not_1_out, a);
  not not_2 (not_2_out, b);
  and and_1 (and_1_out, not_1_out, not_2_out, not_3_out);
  not not_3 (not_3_out, d);
  not not_4 (not_4_out, b);
  and and_2 (and_2_out, not_4_out, c, d);
  and and_3 (and_3_out, b, not_5_out, d);
  not not_5 (not_5_out, c);
  and and_4 (and_4_out, b, c, not_6_out);
  not not_6 (not_6_out, d);
  and and_5 (and_5_out, a, not_7_out, not_8_out);
  not not_7 (not_7_out, c);
  not not_8 (not_8_out, d);
  or or_1 (x, and_1_out, and_2_out, and_3_out, and_4_out, and_5_out);
endmodule

module e (
  input  a,
  input  b,
  input  c,
  input  d,
  output x
);

  wire and_1_out, and_2_out, and_3_out, and_4_out, not_1_out, not_2_out, not_3_out;

  not not_1 (not_1_out, b);
  and and_1 (and_1_out, not_1_out, not_2_out);
  not not_2 (not_2_out, d);
  and and_2 (and_2_out, c, not_3_out);
  not not_3 (not_3_out, d);
  and and_3 (and_3_out, a, c);
  and and_4 (and_4_out, a, b);
  or or_1 (x, and_1_out, and_2_out, and_3_out, and_4_out);
endmodule

module g (
  input  a,
  input  b,
  input  c,
  input  d,
  output x
);

  wire and_1_out, and_2_out, and_3_out, and_4_out, and_5_out, not_1_out, not_2_out, not_3_out, not_4_out,
       not_5_out;

  not not_1 (not_1_out, b);
  and and_1 (and_1_out, not_1_out, c);
  and and_2 (and_2_out, c, not_2_out);
  not not_2 (not_2_out, d);
  not not_3 (not_3_out, a);
  and and_3 (and_3_out, not_3_out, b, not_4_out);
  not not_4 (not_4_out, c);
  and and_4 (and_4_out, a, not_5_out);
  not not_5 (not_5_out, b);
  and and_5 (and_5_out, a, d);
  or or_1 (x, and_1_out, and_2_out, and_3_out, and_4_out, and_5_out);
endmodule

module f (
  input  a,
  input  b,
  input  c,
  input  d,
  output x
);

  wire and_1_out, and_2_out, and_3_out, and_4_out, and_5_out, not_1_out, not_2_out, not_3_out, not_4_out,
       not_5_out, not_6_out;

  not not_1 (not_1_out, c);
  and and_1 (and_1_out, not_1_out, not_2_out);
  not not_2 (not_2_out, d);
  not not_3 (not_3_out, a);
  and and_2 (and_2_out, not_3_out, b, not_4_out);
  not not_4 (not_4_out, c);
  and and_3 (and_3_out, b, not_5_out);
  not not_5 (not_5_out, d);
  and and_4 (and_4_out, a, not_6_out);
  not not_6 (not_6_out, b);
  and and_5 (and_5_out, a, c);
  or or_1 (x, and_1_out, and_2_out, and_3_out, and_4_out, and_5_out);
endmodule
